// Digital circuit subterranean_duplex.dig as structural Verilog
module subterranean_duplex (
  input  [63:0] state_0_63,
  input  [63:0] state_128_191,
  input  [63:0] state_192_255,
  input  [63:0] state_64_127,
  input  [63:0] state_256,
  input  [31:0] sigma,
  output [63:0] state__0_63,
  output [63:0] state__64_127,
  output [63:0] state__128_191,
  output [63:0] state__192_255,
  output state__256
);

  wire or_33_out, subterranean_round_1_p10, undriven, undriven_2, undriven_3;
  wire [35:1] subterranean_round_1_p6;
  wire [47:0] subterranean_round_1_p7;
  wire [56:0] subterranean_round_1_p8;
  wire [57:5] subterranean_round_1_p9;

  // Subterranean_round subterranean_round_1: pin names not known; wires that end beside it: state_0_63, state_64_127, state_128_191, state_192_255, state_256, {state__0_63[63:36], subterranean_round_1_p6[35], state__0_63[34:31], subterranean_round_1_p6[30], state__0_63[29:23], subterranean_round_1_p6[22], state__0_63[21:18], subterranean_round_1_p6[17], state__0_63[16], subterranean_round_1_p6[15], state__0_63[14:12], subterranean_round_1_p6[11], state__0_63[10:5], subterranean_round_1_p6[4], state__0_63[3], subterranean_round_1_p6[2:1], state__0_63[0]}, {state__64_127[63:48], subterranean_round_1_p7[47], state__64_127[46:32], subterranean_round_1_p7[31], state__64_127[30:7], subterranean_round_1_p7[6], state__64_127[5:1], subterranean_round_1_p7[0]}, {state__128_191[63:57], subterranean_round_1_p8[56], state__128_191[55:49], subterranean_round_1_p8[48], state__128_191[47:42], subterranean_round_1_p8[41], state__128_191[40:38], subterranean_round_1_p8[37], state__128_191[36:13], subterranean_round_1_p8[12], state__128_191[11:7], subterranean_round_1_p8[6], state__128_191[5:1], subterranean_round_1_p8[0]}, {state__192_255[63:58], subterranean_round_1_p9[57], state__192_255[56:50], subterranean_round_1_p9[49], state__192_255[48:43], subterranean_round_1_p9[42], state__192_255[41:34], subterranean_round_1_p9[33], state__192_255[32], subterranean_round_1_p9[31], state__192_255[30:22], subterranean_round_1_p9[21], state__192_255[20], subterranean_round_1_p9[19], state__192_255[18:6], subterranean_round_1_p9[5], state__192_255[4:0]}, subterranean_round_1_p10
  or or_1 (state__0_63[1], subterranean_round_1_p6[1], sigma[0]);
  or or_2 (state__0_63[2], subterranean_round_1_p6[2], sigma[1]);
  or or_3 (state__0_63[4], subterranean_round_1_p6[4], sigma[2]);
  or or_4 (state__0_63[11], subterranean_round_1_p6[11], sigma[3]);
  or or_5 (state__0_63[15], subterranean_round_1_p6[15], sigma[4]);
  or or_6 (state__0_63[17], subterranean_round_1_p6[17], sigma[5]);
  or or_7 (state__0_63[22], subterranean_round_1_p6[22], sigma[6]);
  or or_8 (state__0_63[30], subterranean_round_1_p6[30], sigma[7]);
  or or_9 (state__0_63[35], subterranean_round_1_p6[35], sigma[8]);
  or or_10 (state__64_127[0], subterranean_round_1_p7[0], sigma[9]);
  or or_11 (state__64_127[6], subterranean_round_1_p7[6], sigma[10]);
  or or_12 (state__64_127[31], subterranean_round_1_p7[31], sigma[11]);
  or or_13 (state__64_127[47], subterranean_round_1_p7[47], sigma[12]);
  or or_14 (state__128_191[0], subterranean_round_1_p8[0], sigma[13]);
  or or_15 (state__128_191[6], subterranean_round_1_p8[6], sigma[14]);
  or or_16 (state__128_191[8], state__128_191[8], sigma[15]);
  or or_17 (state__128_191[9], state__128_191[9], sigma[16]);
  or or_18 (state__128_191[12], subterranean_round_1_p8[12], sigma[17]);
  or or_19 (state__128_191[37], subterranean_round_1_p8[37], sigma[18]);
  or or_20 (state__128_191[41], subterranean_round_1_p8[41], sigma[19]);
  or or_21 (state__128_191[48], subterranean_round_1_p8[48], sigma[20]);
  or or_22 (state__128_191[56], subterranean_round_1_p8[56], sigma[21]);
  or or_23 (state__128_191[61], state__128_191[61], sigma[22]);
  or or_24 (state__128_191[62], state__128_191[62], sigma[23]);
  or or_25 (state__192_255[5], subterranean_round_1_p9[5], sigma[24]);
  or or_26 (state__192_255[19], subterranean_round_1_p9[19], sigma[25]);
  or or_27 (state__192_255[21], subterranean_round_1_p9[21], sigma[27]);
  or or_28 (state__192_255[31], subterranean_round_1_p9[31], sigma[28]);
  buf or_29 (state__192_255[33], sigma[29]);  // Or open: In_1
  buf or_30 (state__192_255[42], sigma[30]);  // Or open: In_1
  buf or_31 (state__192_255[49], sigma[31]);  // Or open: In_1
  or or_32 (state__192_255[57], undriven, undriven_2);
  or or_33 (or_33_out, undriven_3, subterranean_round_1_p10);
  or or_34 (state__256, 1'b1, or_33_out);
endmodule
